# Fritzing sketch switches (saved by Fritzing 0.9.3b)

parts:
  U1 = NodeMCU V1.0
  JP1 = Header 6 [package=molex-1x6-ra]
  JP2 = Header 6 [package=molex-1x6-ra]
  JP3 = Header 4 [package=screwterminal-3.5mm-4_lock]
  U2 = Sharp PC817 [package=THT]
  U3 = Sharp PC817 [package=THT]
  U4 = Sharp PC817 [package=THT]
  U5 = Sharp PC817 [package=THT]
  R2 = Resistor [tolerance=±5% resistance=150 package=THT]  # not connected
  R3 = Resistor [tolerance=±5% resistance=150 package=THT]  # not connected
  R4 = Resistor [tolerance=±5% resistance=150 package=THT]  # not connected
  R5 = Resistor [tolerance=±5% resistance=150 package=THT]  # not connected
  R6 = Resistor [tolerance=±5% resistance=10k package=THT]
  U6 = Buck Converter [package=odfn6]

nets:
  N1: U1.D2, U5.Pin_1
  N2: U1.D5, JP1.2, R6.Pin_0
  N3: U1.D6, U4.Pin_1
  N4: U1.D7, U3.Pin_1
  N5: U1.D8, U2.Pin_1
  N6: U1.GND, U6.Roomba_+
  N7: U1.A0, JP2.2
  N8: JP1.1, JP1.3, U5.Pin_4, U5.Pin_3
  N9: JP1.4, U4.Pin_4
  N10: JP1.5, U3.Pin_4
  N11: JP1.6, U2.Pin_4
  N12: JP3.1, U6.ESP_-
  N13: JP3.4, U6.Roomba_-

notes:
  Com Port
  Spa
  Side
  Temp
  Sensor
  10k pulldown
  resistor on D5

custom parts:
  NodeMCU V1.0: ESP8266 based NodeMCU
